// Logisim project Datapath.circ as structural Verilog: 2 circuits, main circuit main
module main (
  input  in_1,
  input  in_2
);

  wire AluSrc, and_1_out, Bne, Branch, clock_1_out, decodificador_1_p1, extensor_sinal_1_p1, Jump,
       JumpRegister, Link, main_1_p3, main_2_p1, main_3_p8, MemRead, MemToReg, MemWrite, multiplexer_4_out,
       not_1_out, not_2_out, RegDst, WriteReg, zero;
  wire [4:0] decodificador_1_p2, decodificador_1_p3, main_3_p3, multiplexer_5_out, Op, shamt;
  wire [5:0] OpCode;
  wire [25:0] decodificador_1_p4;
  wire [31:0] adder_1_out, datamem_1_p7, extensor_sinal_1_p2, extensor_sinal_1_p3, LD1, main_3_p6, main_4_p5,
       meminstr_1_instruction, multiplexer_1_out, multiplexer_2_out, multiplexer_3_out, multiplexer_7_out,
       multiplexer_9_out, PC, pc___4, pseudodireto_1_saida, shifter_1_out;

  // Probe on multiplexer_3_out
  Multiplexer #(.width(32), .enable("false")) multiplexer_1 (
    .in0(multiplexer_3_out), .in1(LD1), .out(multiplexer_1_out), .sel(JumpRegister));
  // Probe on pseudodireto_1_saida
  Multiplexer #(.width(32), .enable("false")) multiplexer_2 (
    .in0(multiplexer_1_out), .in1(pseudodireto_1_saida), .out(multiplexer_2_out), .sel(Jump));
  pseudodireto pseudodireto_1 (.PC(PC), .Saida(pseudodireto_1_saida), .addr(decodificador_1_p4));
  // Probe on multiplexer_2_out
  // Probe on extensor_sinal_1_p2
  Multiplexer #(.width(32), .enable("false")) multiplexer_3 (
    .in0(pc___4), .in1(adder_1_out), .out(multiplexer_3_out), .sel(and_1_out));
  Multiplexer #(.enable("false")) multiplexer_4 (.in0(zero), .in1(not_1_out), .out(multiplexer_4_out), .sel(Bne));
  not not_1 (not_1_out, zero);
  Register #(.width(32)) u_PC (.D(multiplexer_2_out), .en(1'b1), .Q(PC), .clk(clock_1_out), .clr(in_1));
  Clock clock_1 (.out(clock_1_out));
  Shifter #(.width(32)) shifter_1 (.in(extensor_sinal_1_p2), .\dist (5'b00010), .out(shifter_1_out));
  Adder #(.width(32)) adder_1 (.a(shifter_1_out), .b(pc___4), .out(adder_1_out));  // open: cin, cout
  and and_1 (and_1_out, multiplexer_4_out, Branch);
  Adder #(.width(32)) adder_2 (.a(32'h4), .b(PC), .out(pc___4));  // open: cin, cout
  MemInstr meminstr_1 (.PC_address(PC), .Instruction(meminstr_1_instruction));
  // Probe on meminstr_1_instruction
  // Probe on main_1_p3
  // UC_main main_1: pin names not known; wires that end beside it: meminstr_1_instruction, OpCode, main_1_p3, OpCode, MemRead, MemWrite, Branch, Bne, Jump, Link
  // extensor_sinal extensor_sinal_1: pin names not known; wires that end beside it: extensor_sinal_1_p1, extensor_sinal_1_p2, extensor_sinal_1_p3
  // decodificador decodificador_1: pin names not known; wires that end beside it: decodificador_1_p1, decodificador_1_p2, decodificador_1_p3, decodificador_1_p4, extensor_sinal_1_p1, shamt
  // UCA_main main_2: pin names not known; wires that end beside it: main_2_p1, RegDst, WriteReg, AluSrc, MemToReg, main_1_p3, OpCode, main_2_p1, Op, JumpRegister
  Multiplexer #(.width(5), .enable("false")) multiplexer_5 (
    .in0(decodificador_1_p2), .in1(decodificador_1_p3), .out(multiplexer_5_out), .sel(RegDst));
  // Registers_Bank_main main_3: pin names not known; wires that end beside it: decodificador_1_p1, decodificador_1_p2, main_3_p3, clock_1_out, LD1, main_3_p6, in_1, main_3_p8
  Multiplexer #(.width(5), .enable("false")) multiplexer_6 (
    .in0(multiplexer_5_out), .in1({5{1'b1}}), .out(main_3_p3), .sel(Link));
  and and_2 (main_3_p8, not_2_out, WriteReg);
  not not_2 (not_2_out, JumpRegister);
  Multiplexer #(.width(32), .enable("false")) multiplexer_7 (
    .in0(main_3_p6), .in1(extensor_sinal_1_p2), .out(multiplexer_7_out), .sel(AluSrc));
  // Probe on LD1
  // Probe on multiplexer_7_out
  Multiplexer #(.width(32), .enable("false")) multiplexer_8 (
    .in0(multiplexer_9_out), .in1(pc___4), .out(extensor_sinal_1_p3), .sel(Link));
  // Probe on main_3_p6
  Multiplexer #(.width(32), .enable("false")) multiplexer_9 (
    .in0(main_4_p5), .in1(datamem_1_p7), .out(multiplexer_9_out), .sel(MemToReg));
  // Probe on main_4_p5
  // ULA_main main_4: pin names not known; wires that end beside it: LD1, multiplexer_7_out, shamt, Op, main_4_p5, zero
  // datamem datamem_1: pin names not known; wires that end beside it: main_4_p5, main_3_p6, MemRead, MemWrite, clock_1_out, in_2, datamem_1_p7

  // Other names for the same wires on the sheet: Reset = in_1
endmodule

module pseudodireto (
  input  [25:0] addr,
  input  [31:0] PC,
  output [31:0] Saida
);

  // Probe on addr
  Shifter #(.width(26)) shifter_1 (.in(addr), .\dist (5'b00010), .out(Saida[25:0]));
  // Probe on Saida[25:0]

  assign Saida[31:26] = PC[31:26];
endmodule
