// Logisim project meminstr.circ as structural Verilog: 1 circuit, main circuit MemInstr
module MemInstr (
  input  [31:0] PC_address,
  output [31:0] Instruction
);

  // Probe on PC_address
  // Probe on PC_address[25:2]
  ROM #(.addrWidth(24), .dataWidth(32)) rom_1 (.addr(PC_address[25:2]), .data(Instruction));  // open: sel
  // Probe on Instruction

  // Notes on the sheet:
  //   contents of rom_1 (hex, n*v repeats v):
  //   0 2010001e 2004004 20090001 11090005 2305002 ad500000 2210ffff 8000002 2534002 ae480000 2519002
  //   2534002 ae480000 2519002 2534002 ae480000 2519002 2534002 ae480000 2519002 2534002 ae480000 2519002
  //   2534002 ae480000 25190002 2534002 ae480000 2519002 2534002 ae480000 2519002 2534002 ae480000 2519002
  //   2534002 ae480000 262106*0 12312 14*0 aed 3932144*0 dea
endmodule
